# Fritzing sketch schematic (saved by Fritzing 0.9.3b)
breadboards: 1
perfboards: 1

parts:
  WeMos_D1_Mini1 = WeMos D1 Mini  # not connected
  Q1 = NPN-Transistor [package="TO92 [THT]"]
  Q2 = NPN-Transistor [package="TO92 [THT]"]
  Q3 = NPN-Transistor [package="TO92 [THT]"]
  J1 = male pin header, 2 pins [form="♂ (male)"]
  J2 = male pin header, 1 pin [form="♂ (male)"]
  R1 = Resistor [tolerance=±5% resistance=10k package=THT]
  R2 = Resistor [tolerance=±5% resistance=1k package=THT]  # not connected
  J3 = male pin header, 2 pins [form="♂ (male)"]
  J4 = male pin header, 2 pins [form="♂ (male)"]
  J5 = male pin header, 2 pins [form="♂ (male)"]
  J6 = male pin header, 2 pins [form="♂ (male)"]
  R3 = Resistor [tolerance=±5% resistance=560 package=THT]
  R4 = Resistor [tolerance=±5% resistance=560 package=THT]
  R5 = Resistor [tolerance=±2% resistance=1k package=THT]
  J7 = female pin header, 2 pins [form="♀ (female)"]
  DHT1 = DHT11 Humitidy and Temperature Sensor
  WeMos_D1_Mini2 = WeMos D1 Mini
  DHT2 = DHT11 Humitidy and Temperature Sensor
  J11 = rounded female pin header, 5 pins [form="♀ (female rounded)"]
  J8 = double row male pin header, 6 pins [form="♂ (male)"]
  J12 = rounded female pin header, 2 pins [form="♀ (female rounded)"]
  R6 = Resistor [tolerance=±5% resistance=220 package="1206 [SMD]"]
  R7 = Resistor [tolerance=±5% resistance=220 package="1206 [SMD]"]
  R8 = Resistor [tolerance=±5% resistance=220 package="1206 [SMD]"]
  R9 = Resistor [tolerance=±5% resistance=220 package="1206 [SMD]"]
  R10 = Resistor [tolerance=±5% resistance=220 package="1206 [SMD]"]
  R11 = Resistor [tolerance=±5% resistance=220 package="1206 [SMD]"]
  Q4 = NPN-Transistor [package="TO92 [THT]"]
  Q6 = NPN-Transistor [package="TO92 [THT]"]
  Q7 = NPN-Transistor [package="TO92 [THT]"]

nets:
  N1: Q1.E, R5.Pin_0
  N2: Q1.B, R3.Pin_1
  N3: Q1.C, Q2.C, Q3.C, J1.pin2, J7.pin2, DHT1.GND
  N4: Q2.E, J5.pin1, J6.pin1
  N5: Q2.B, R4.Pin_1
  N6: Q3.B, R1.Pin_0
  N7: J1.pin1, J2.pin1, R1.Pin_1
  N8: J3.pin1, J4.pin1, R5.Pin_1
  N9: J3.pin2, J4.pin2
  N10: J5.pin2, J6.pin2
  N11: J7.pin1, DHT1.VDD
  N12: WeMos_D1_Mini2.3V3, R7.Pin_0
  N13: WeMos_D1_Mini2.D4, DHT2.DATA
  N14: WeMos_D1_Mini2.D5, R10.Pin_0
  N15: WeMos_D1_Mini2.D6, R7.Pin_1, Q6.C
  N16: WeMos_D1_Mini2.D7, R11.Pin_0
  N17: DHT2.VDD, J12.pin1
  N18: DHT2.GND, J8.pin1, J12.pin2
  N19: J11.pin1, R6.Pin_1
  N20: J11.pin2, J8.pin3
  N21: J11.pin3, R8.Pin_0
  N22: J11.pin4, J8.pin5
  N23: J11.pin5, R9.Pin_0
  N24: R6.Pin_0, Q6.B
  N25: R8.Pin_1, Q7.C
  N26: R9.Pin_1, Q4.C
  N27: R10.Pin_1, Q7.B
  N28: R11.Pin_1, Q4.B

notes:
  Red line +5V
  Orange +3.3V
  Connectors
  MB pins: pwled+ pwbtn+- rstbtn+-
  PC parts: pwled pwbtn rstbtn
  Connector
  MB: +5VSB GND
  pwled power reset
  MB +-+-+
  led/btns -+-+-+
  +5VSB GND

custom parts:
  DHT11 Humitidy and Temperature Sensor: DHT11 Humidity and Temperature Sensor
